// Digital circuit Main.dig as structural Verilog
module Main (
  input  clk,
  input  in_3,
  input  in_4,
  input  in_5,
  input  in_6,
  input  in_7,
  input  in_8,
  input  in_9,
  input  in_10,
  input  in_11,
  input  in_12,
  input  in_13,
  input  in_14,
  input  in_15,
  input  in_16,
  input  in_17,
  input  in_18,
  input  in_19,
  input  in_20,
  input  in_21,
  input  in_22,
  input  in_23,
  input  in_24,
  input  in_25,
  input  in_26,
  input  in_27,
  input  in_28,
  input  in_29,
  input  in_30,
  input  in_31,
  input  in_32,
  input  in_33,
  input  in_34,
  input  in_35,
  input  in_36,
  input  in_37,
  input  in_38,
  input  in_39,
  input  in_40,
  input  in_41,
  input  in_42,
  input  in_43,
  input  in_44,
  input  in_45,
  input  in_46,
  input  in_47,
  input  in_48,
  input  clk_2,
  output [7:0] out
);

  wire comparator_1_eq, comparator_1_gt, comparator_1_lt, comparator_2_eq, comparator_3_eq, comparator_4_eq,
       comparator_5_eq, comparator_6_eq, comparator_7_eq, comparator_8_lt, comparator_9_lt, decoder_1_out_0,
       decoder_1_out_17, decoder_2_out_0, decoder_2_out_2, decoder_3_out_0, decoder_3_out_2, decoder_4_out_0,
       decoder_4_out_1, decoder_4_out_2, multiplexer_3_out, not_2_out, or_2_out, or_3_out, or_5_out,
       or_7_out, priorityencoder_1_any, priorityencoder_2_any, priorityencoder_2_num, priorityencoder_3_any,
       rs_ff_as_1_nq, rs_ff_as_2_nq;
  wire [0:0] and_2_out;
  wire [1:0] decoder_1_out_9, rom_1_d_5;
  wire [2:0] priorityencoder_1_num, priorityencoder_3_num;
  wire [5:0] decoder_1_out_11;
  wire [7:0] add_1_s, and_1_out, counterpreset_1_out, decoder_1_out_1, demultiplexer_1_out_0,
       demultiplexer_1_out_1, demultiplexer_2_out_0, demultiplexer_3_out_0, demultiplexer_4_out_0,
       demultiplexer_4_out_1, demultiplexer_5_out_0, demultiplexer_5_out_1, demultiplexer_5_out_2,
       demultiplexer_6_out_0, demultiplexer_6_out_1, demultiplexer_7_out_0, demultiplexer_7_out_1, div_1_q,
       Left_out, Memory_d2, mul_1_mul, multiplexer_1_out, multiplexer_2_out, multiplexer_4_out,
       multiplexer_5_out, not_1_out, or_1_out, or_4_out, or_6_out, or_8_out, or_9_out, Right_out, rom_1_d_4,
       stack_1_out, sub_1_s, switch_1_out, switch_2_out, switch_3_out, Video_d2, xor_1_out;
  wire [9:0] rom_1_d_2, rom_1_d_3;
  wire [11:0] counter_1_out, counter_2_out, driver_1_out, driver_2_out;
  wire [11:8] div_2_q_2, div_3_q;
  wire [15:0] div_2_q, rom_1_d;
  wire [15:8] mul_1_mul_2;

  Add #(.Bits(8)) add_1 (.a(multiplexer_4_out), .b(multiplexer_5_out), .c_i(1'b0), .s(add_1_s));  // open: c_o
  Sub #(.Bits(8)) sub_1 (.a(multiplexer_4_out), .b(multiplexer_5_out), .c_i(1'b0), .s(sub_1_s));  // open: c_o
  Mul #(.Signed("true"), .Bits(8)) mul_1 (.a(multiplexer_4_out), .b(multiplexer_5_out), .mul({mul_1_mul_2, mul_1_mul}));
  Div #(.Bits(8)) div_1 (.a(multiplexer_4_out), .b(multiplexer_5_out), .q(div_1_q));  // open: r
  assign and_1_out = multiplexer_4_out & multiplexer_4_out;  // And and_1, 8 bits wide
  assign not_1_out = ~multiplexer_4_out;  // Not not_1, 8 bits wide
  assign or_1_out = multiplexer_4_out | multiplexer_4_out;  // Or or_1, 8 bits wide
  assign xor_1_out = multiplexer_4_out ^ multiplexer_4_out;  // XOr xor_1, 8 bits wide
  CounterPreset #(.Bits(8), .isProgramCounter("true")) counterpreset_1 (
    .en(1'b1), .C(clk_2), .dir(1'b0), .in(multiplexer_4_out), .ld(decoder_1_out_17), .clr(1'b0),
    .out(counterpreset_1_out));  // open: ovf
  Multiplexer #(.Selector_Bits(3), .Bits(8)) multiplexer_1 (
    .sel(priorityencoder_1_num), .in_0(add_1_s), .in_1(sub_1_s), .in_2(mul_1_mul), .in_3(div_1_q),
    .in_4(and_1_out), .in_5(not_1_out), .in_6(or_1_out), .in_7(xor_1_out), .out(multiplexer_1_out));
  PriorityEncoder #(.Selector_Bits(3)) priorityencoder_1 (
    .in0(decoder_1_out_1[0]), .in1(decoder_1_out_1[1]), .in2(decoder_1_out_1[2]), .in3(decoder_1_out_1[3]),
    .in4(decoder_1_out_1[4]), .in5(decoder_1_out_1[5]), .in6(decoder_1_out_1[6]), .in7(decoder_1_out_1[7]),
    .num(priorityencoder_1_num), .any(priorityencoder_1_any));
  // Probe on counterpreset_1_out
  ROM #(.AddrBits(8), .isProgramMemory("true"), .Bits(46)) rom_1 (
    .A(counterpreset_1_out), .sel(1'b1), .D({rom_1_d_5, rom_1_d_4, rom_1_d_3, rom_1_d_2, rom_1_d}));
  Switch switch_1 (.in(multiplexer_1_out), .send(priorityencoder_1_any), .out(switch_1_out));
  PullDown #(.Bits(46)) pulldown_1 (.out({rom_1_d_5, rom_1_d_4, rom_1_d_3, rom_1_d_2, rom_1_d}));
  Decoder #(.Selector_Bits(5)) decoder_1 (
    .sel(rom_1_d[4:0]), .out_0(decoder_1_out_0), .out_1(decoder_1_out_1[0]), .out_2(decoder_1_out_1[1]),
    .out_3(decoder_1_out_1[2]), .out_4(decoder_1_out_1[3]), .out_5(decoder_1_out_1[4]),
    .out_6(decoder_1_out_1[5]), .out_7(decoder_1_out_1[6]), .out_8(decoder_1_out_1[7]),
    .out_9(decoder_1_out_9[0]), .out_10(decoder_1_out_9[1]), .out_11(decoder_1_out_11[0]),
    .out_12(decoder_1_out_11[1]), .out_13(decoder_1_out_11[2]), .out_14(decoder_1_out_11[3]),
    .out_15(decoder_1_out_11[4]), .out_16(decoder_1_out_11[5]), .out_17(decoder_1_out_17));  // open: out_18, out_19, out_20, out_21, out_22, out_23, out_24, out_25, out_26, out_27, out_28, out_29, out_30, out_31
  BarrelShifter #(.Bits(8)) Left (.in(demultiplexer_1_out_0), .shift(4'b0001), .out(Left_out));
  Demultiplexer #(.Bits(8)) demultiplexer_1 (
    .sel(priorityencoder_2_num), .in(multiplexer_4_out), .out_0(demultiplexer_1_out_0),
    .out_1(demultiplexer_1_out_1));
  PriorityEncoder priorityencoder_2 (
    .in0(decoder_1_out_9[0]), .in1(decoder_1_out_9[1]), .num(priorityencoder_2_num),
    .any(priorityencoder_2_any));
  BarrelShifter #(.Bits(8), .direction("right")) Right (.in(demultiplexer_1_out_1), .shift(4'b0001), .out(Right_out));
  Multiplexer #(.Bits(8)) multiplexer_2 (
    .sel(priorityencoder_2_num), .in_0(Right_out), .in_1(Left_out), .out(multiplexer_2_out));
  Switch switch_2 (.in(multiplexer_2_out), .send(priorityencoder_2_any), .out(switch_2_out));
  Comparator #(.Signed("true"), .Bits(8)) comparator_1 (
    .a(multiplexer_4_out), .b(multiplexer_5_out), .gt(comparator_1_gt), .eq(comparator_1_eq),
    .lt(comparator_1_lt));
  not not_2 (not_2_out, comparator_1_eq);
  or or_2 (or_2_out, comparator_1_lt, comparator_1_eq);
  or or_3 (or_3_out, comparator_1_gt, comparator_1_eq);
  Multiplexer #(.Selector_Bits(3)) multiplexer_3 (
    .sel(priorityencoder_3_num), .in_0(comparator_1_eq), .in_1(not_2_out), .in_2(or_2_out),
    .in_3(comparator_1_gt), .in_4(or_3_out), .in_5(1'b0), .in_6(1'b0), .in_7(1'b0), .out(multiplexer_3_out));
  PriorityEncoder #(.Selector_Bits(3)) priorityencoder_3 (
    .in0(decoder_1_out_11[0]), .in1(decoder_1_out_11[1]), .in2(decoder_1_out_11[2]),
    .in3(decoder_1_out_11[3]), .in4(decoder_1_out_11[4]), .in5(decoder_1_out_11[5]), .in6(1'b0), .in7(1'b0),
    .num(priorityencoder_3_num), .any(priorityencoder_3_any));
  Switch switch_3 (.in(multiplexer_4_out), .send(decoder_1_out_0), .out(switch_3_out));
  and and_2 (and_2_out[0], multiplexer_3_out, priorityencoder_3_any);
  Multiplexer #(.Bits(8)) multiplexer_4 (
    .sel(rom_1_d[14]), .in_0(or_9_out), .in_1(rom_1_d_2[7:0]), .out(multiplexer_4_out));
  Multiplexer #(.Bits(8)) multiplexer_5 (
    .sel(rom_1_d[15]), .in_0(or_8_out), .in_1(rom_1_d_3[7:0]), .out(multiplexer_5_out));
  assign or_4_out = {{7{1'b0}}, and_2_out[0]} | switch_1_out | switch_2_out | switch_3_out;  // Or or_4, 8 bits wide
  Demultiplexer #(.Selector_Bits(2), .Bits(8)) demultiplexer_2 (
    .sel(rom_1_d_2[9:8]), .in(rom_1_d_2[7:0]), .out_0(demultiplexer_2_out_0));  // open: out_1, out_2, out_3
  Decoder #(.Selector_Bits(2)) decoder_2 (
    .sel(rom_1_d_2[9:8]), .out_0(decoder_2_out_0), .out_2(decoder_2_out_2));  // open: out_1, out_3
  Demultiplexer #(.Selector_Bits(2), .Bits(8)) demultiplexer_3 (
    .sel(rom_1_d_3[9:8]), .in(rom_1_d_3[7:0]), .out_0(demultiplexer_3_out_0));  // open: out_1, out_2, out_3
  Decoder #(.Selector_Bits(2)) decoder_3 (
    .sel(rom_1_d_3[9:8]), .out_0(decoder_3_out_0), .out_2(decoder_3_out_2));  // open: out_1, out_3
  Demultiplexer #(.Selector_Bits(2), .Bits(8)) demultiplexer_4 (
    .sel(rom_1_d_5), .in(rom_1_d_4), .out_0(demultiplexer_4_out_0), .out_1(demultiplexer_4_out_1));  // open: out_2, out_3
  Decoder #(.Selector_Bits(2)) decoder_4 (
    .sel(rom_1_d_5), .out_0(decoder_4_out_0), .out_1(decoder_4_out_1), .out_2(decoder_4_out_2));  // open: out_3
  Demultiplexer #(.Selector_Bits(2), .Bits(8)) demultiplexer_5 (
    .sel(rom_1_d_5), .in(or_4_out), .out_0(demultiplexer_5_out_0), .out_1(demultiplexer_5_out_1),
    .out_2(demultiplexer_5_out_2), .out_3(out));
  or or_5 (or_5_out, decoder_2_out_2, decoder_3_out_2);
  assign or_6_out = demultiplexer_2_out_0 | demultiplexer_3_out_0;  // Or or_6, 8 bits wide
  or or_7 (or_7_out, decoder_2_out_0, decoder_3_out_0);
  Counter #(.Bits(12)) counter_1 (.en(1'b1), .C(clk), .clr(comparator_4_eq), .out(counter_1_out));  // open: ovf
  Counter #(.Bits(12)) counter_2 (
    .en(1'b1), .C(comparator_4_eq), .clr(comparator_7_eq), .out(counter_2_out));  // open: ovf
  Comparator #(.Bits(12)) comparator_2 (.a(counter_1_out), .b(12'h290), .eq(comparator_2_eq));  // open: gt, lt
  Comparator #(.Bits(12)) comparator_3 (.a(counter_1_out), .b(12'h2f0), .eq(comparator_3_eq));  // open: gt, lt
  Comparator #(.Bits(12)) comparator_4 (.a(counter_1_out), .b(12'h31f), .eq(comparator_4_eq));  // open: gt, lt
  Comparator #(.Bits(12)) comparator_5 (.a(counter_2_out), .b(12'h1ea), .eq(comparator_5_eq));  // open: gt, lt
  Comparator #(.Bits(12)) comparator_6 (.a(counter_2_out), .b(12'h1ec), .eq(comparator_6_eq));  // open: gt, lt
  Comparator #(.Bits(12)) comparator_7 (.a(counter_2_out), .b(12'h20c), .eq(comparator_7_eq));  // open: gt, lt
  RS_FF_AS rs_ff_as_1 (.S(comparator_2_eq), .R(comparator_3_eq), .nQ(rs_ff_as_1_nq));  // open: Q
  RS_FF_AS rs_ff_as_2 (.S(comparator_5_eq), .R(comparator_6_eq), .nQ(rs_ff_as_2_nq));  // open: Q
  RAMDualAccess #(.AddrBits(8), .Bits(8)) Memory (
    .str(decoder_4_out_0), .C(clk_2), .ld(or_7_out), .A1(demultiplexer_4_out_0),
    .Din1(demultiplexer_5_out_0), .A2(or_6_out), .D2(Memory_d2));  // open: D1
  RAMDualAccess #(.AddrBits(16), .Bits(8)) Video (
    .str(decoder_4_out_1), .C(clk_2), .ld(1'b1),
    .A1({4'b0000, demultiplexer_4_out_1[7:4], 4'b0000, demultiplexer_4_out_1[3:0]}),
    .Din1(demultiplexer_5_out_1), .A2(div_2_q), .D2(Video_d2));  // open: D1
  Stack stack_1 (
    .clock(clk_2), .pop(or_5_out), .push(decoder_4_out_2), .pushD(demultiplexer_5_out_2), .out(stack_1_out));
  Demultiplexer #(.Bits(8)) demultiplexer_6 (
    .sel(decoder_3_out_0), .in(Memory_d2), .out_0(demultiplexer_6_out_0), .out_1(demultiplexer_6_out_1));
  Demultiplexer #(.Bits(8)) demultiplexer_7 (
    .sel(decoder_3_out_2), .in(stack_1_out), .out_0(demultiplexer_7_out_0), .out_1(demultiplexer_7_out_1));
  Comparator #(.Bits(12)) comparator_8 (.a(counter_1_out), .b(12'h280), .lt(comparator_8_lt));  // open: gt, eq
  Comparator #(.Bits(12)) comparator_9 (.a(counter_2_out), .b(12'h1e0), .lt(comparator_9_lt));  // open: gt, eq
  assign or_8_out = demultiplexer_6_out_0 | demultiplexer_7_out_0;  // Or or_8, 8 bits wide
  assign or_9_out = demultiplexer_6_out_1 | demultiplexer_7_out_1;  // Or or_9, 8 bits wide
  Div #(.Bits(12)) div_2 (.a(driver_1_out), .b(12'h4), .q({div_2_q_2, div_2_q[7:0]}));  // open: r
  assign driver_1_out = comparator_8_lt ? counter_1_out : 12'bz;  // Driver driver_1
  Div #(.Bits(12)) div_3 (.a(driver_2_out), .b(12'h4), .q({div_3_q, div_2_q[15:8]}));  // open: r
  assign driver_2_out = comparator_9_lt ? counter_2_out : 12'bz;  // Driver driver_2
  VGA vga_1 (.R(Video_d2[1:0]), .G(Video_d2[3:2]), .B(Video_d2[5:4]), .H(rs_ff_as_1_nq), .V(rs_ff_as_2_nq), .C(clk));

  // Notes on the sheet:
  //   clk: Hz: 2147483647
  //   clk_2: Hz: 100
  //   Output Addresses 1
  //   Input Addresses 2
  //   Input Addresses 1
  //   OP Code
  //   ALU
  //   contents of rom_1 (hex, n*v repeats v):
  //   1110003f4000,1210003f4000,1310003f4000,1220003f4000,1230003f4000
  //   ,1330003f4000,1130003f4000,1410003f4000,1430003f4000,1150003f4000
  //   ,1350003f4000,1450003f4000
  //   INTERMEDIATE
  //   COPY
  //   SHIFT
  //   COMPARE
  //   JUMP
  //   01
  //   10
  //   11
endmodule
