// Digital circuit Stack.dig as structural Verilog
module Stack (
  input  clock,
  input  pop,
  input  push,
  input  [7:0] pushD,
  output [7:0] out
);

  wire or_1_out;
  wire [7:0] add_1_s, multiplexer_1_out, multiplexer_2_out, register_1_q, sub_1_s, switch_1_out, switch_2_out;

  or or_1 (or_1_out, push, pop);
  Switch switch_1 (.in({8{1'b1}}), .send(push), .out(switch_1_out));
  Switch switch_2 (.in({8{1'b1}}), .send(pop), .out(switch_2_out));
  Register #(.Bits(8)) register_1 (.D(multiplexer_2_out), .C(clock), .en(or_1_out), .Q(register_1_q));
  Add #(.Bits(8)) add_1 (.a(register_1_q), .b(switch_1_out), .c_i(1'b0), .s(add_1_s));  // open: c_o
  Sub #(.Bits(8)) sub_1 (.a(register_1_q), .b(switch_2_out), .c_i(1'b0), .s(sub_1_s));  // open: c_o
  // Probe on pushD
  // Probe on sub_1_s
  Multiplexer #(.Bits(8)) multiplexer_1 (
    .sel(pop), .in_0(multiplexer_2_out), .in_1(register_1_q), .out(multiplexer_1_out));
  // Probe on add_1_s
  Multiplexer #(.Bits(8)) multiplexer_2 (.sel(pop), .in_0(add_1_s), .in_1(sub_1_s), .out(multiplexer_2_out));
  RAMDualPort #(.AddrBits(8), .isProgramMemory("true"), .Bits(8)) ramdualport_1 (
    .A(multiplexer_1_out), .Din(pushD), .str(push), .C(clock), .ld(pop), .D(out));
endmodule
