// Digital circuit Switch 10 Bit.dig as structural Verilog
module Switch_10_Bit (
  input  [9:0] in,
  input  send,
  output [9:0] out
);

  Multiplexer #(.Bits(10)) multiplexer_1 (.sel(send), .in_0({10{1'b0}}), .in_1(in), .out(out));

  // Notes on the sheet:
  //   send: If 1, let in through, otherwise just send out 0.
endmodule
