// Digital circuit Switch.dig as structural Verilog
module Switch (
  input  [7:0] in,
  input  send,
  output [7:0] out
);

  Multiplexer #(.Bits(8)) multiplexer_1 (.sel(send), .in_0({8{1'b0}}), .in_1(in), .out(out));

  // Notes on the sheet:
  //   send: If 1, let in through, otherwise just send out 0.
endmodule
